# Fritzing sketch ArduinoScheme (saved by Fritzing 0.9.3b)
breadboards: 1

parts:
  R1 = Resistor [tolerance=±5% resistance=220 package=THT]
  LED_Camera_OFF = LED - 5mm [color="Red (633nm)" package="5 mm [THT]"]
  Recepteur_IR = TSOP312.., 314.. [package=THT]
  Led_Camera_ON = LED - 5mm [color="Green (560nm)" package="5 mm [THT]"]
  R2 = Resistor [tolerance=±5% resistance=220 package=THT]
  Power_plug1 = Power plug
  IC1 = L293D [package=THT]
  Ventilateur = DC Motor
  LCD1 = LCD screen
  R3 = TRIMPOT [package=trimpot_tc33]
  Thermistore = Temperature Sensor (Thermistor) [thermistor_type=NTC package=THT]
  R_Thermomètre = Resistor [tolerance=±5% resistance=10 package="1206 [SMD]"]
  WIFI = ESP8266 WiFi Module [part_number=ESP8266]
  MEGA = Arduino Mega 2560 (Rev3)
  A1 = HuskyLens-Vision-Sensor_1
  Transistor_Caméra = NPN-Transistor [package="TO92 [THT]"]
  R4 = Resistor [tolerance=±5% resistance=220 package=THT]
  Bouton_Alimentation = SWITCH-MOMENTARY-2 [package=tactile-pth]

nets:
  N1: R1.Pin_0, Led_Camera_ON.anode
  N2: R1.Pin_1, MEGA.D33
  GND: LED_Camera_OFF.cathode, Recepteur_IR.GND, Led_Camera_ON.cathode, Power_plug1.GND, IC1.0V, LCD1.VSS, LCD1.R/W, LCD1.LED-, R3.CW, R_Thermomètre.Pin_0, WIFI.GND, MEGA.GND, A1.pin3
  N3: LED_Camera_OFF.anode, R2.Pin_0
  N4: Recepteur_IR.Vs, MEGA.D2_PWM
  N5: Recepteur_IR.Data, MEGA.D3_PWM
  N6: R2.Pin_1, MEGA.D11_PWM
  N7: Power_plug1.VCC, IC1.+Vmotor
  N8: IC1.Enable_1, MEGA.D6_PWM
  N9: IC1.In_1, MEGA.D5_PWM
  N10: IC1.Out_1_(_Controlled_by_Enable_1_), Ventilateur.pin_1
  N11: IC1.Out_2_(_Controlled_by_Enable_1_), Ventilateur.pin_2
  N12: IC1.In_2, MEGA.D7_PWM
  VDD: LCD1.VDD, LCD1.LED+, R3.CCW, Thermistore.pin_0, MEGA.5V, Transistor_Caméra.C, Bouton_Alimentation.2
  N13: LCD1.V0, R3.WIPER
  N14: LCD1.RS, MEGA.D26
  N15: LCD1.E, MEGA.D27
  N16: LCD1.DB4, MEGA.D28
  N17: LCD1.DB5, MEGA.D29
  N18: LCD1.DB6, MEGA.D30
  N19: LCD1.DB7, MEGA.D31
  N20: Thermistore.pin_1, R_Thermomètre.Pin_1, MEGA.A0
  N21: WIFI.RXD, MEGA.D36
  VCC: WIFI.VCC, MEGA.3V3
  N22: WIFI.CH_PD, MEGA.D34
  N23: WIFI.TXD, MEGA.D35
  N24: WIFI.REST, MEGA.D37
  N25: MEGA.D21/SCL, MEGA.SCL, A1.pin2
  N26: MEGA.D20/SDA, MEGA.SDA, A1.pin1
  N27: MEGA.D10_PWM, R4.Pin_1
  N28: MEGA.D9_PWM, Bouton_Alimentation.1
  N29: A1.pin4, Transistor_Caméra.E
  N30: Transistor_Caméra.B, R4.Pin_0

custom parts:
  HuskyLens-Vision-Sensor_1: Huskylens is an easy-to-use AI Camera | Vision Sensor. DFrobot Huskylens is equipped with multiple functions, such as face recognition, object tracking, object recognition, line tracking, color recognition, and tag(QR code) recognition.
